// Logisim project PC.circ as structural Verilog: 6 circuits, main circuit main
module main (
  input  in_1,
  input  in_2,
  input  in_3,
  input  in_4,
  input  in_5,
  input  in_6,
  input  in_7,
  input  in_8,
  input  in_9,
  input  in_10,
  input  in_11,
  input  in_12,
  input  in_13,
  input  in_14,
  input  in_15,
  input  in_16,
  input  in_17,
  input  in_18,
  input  in_19,
  input  in_20,
  input  in_21,
  input  in_22,
  input  in_23,
  input  in_24,
  input  in_25,
  input  in_26,
  output out_27
);

  wire alu_1_out_18, alu_1_out_19, alu_1_out_20, alu_1_out_21, alu_1_out_22, alu_1_out_23, alu_1_out_24,
       alu_1_out_25, and_1_out, and_2_out, clock_1_out, clock_2_out, clock_3_out, clock_4_out,
       controlled_buffer_1_out, controlled_buffer_2_out, controlled_buffer_3_out, controlled_buffer_4_out,
       controlled_buffer_5_out, controlled_buffer_6_out, controlled_buffer_7_out, controlled_buffer_8_out,
       controlled_buffer_17_out, controlled_buffer_18_out, controlled_buffer_21_out,
       controlled_buffer_22_out, controlled_buffer_25_out, controlled_buffer_26_out,
       controlled_buffer_27_out, controlled_buffer_28_out, controlled_buffer_33_out,
       controlled_buffer_34_out, controlled_buffer_35_out, controlled_buffer_36_out,
       controlled_buffer_41_out, controlled_buffer_42_out, controlled_buffer_43_out,
       controlled_buffer_46_out, controlled_buffer_47_out, controlled_buffer_48_out, not_1_out,
       register_1_out_10, register_1_out_11, register_1_out_12, register_1_out_13, register_1_out_14,
       register_1_out_15, register_1_out_16, register_1_out_17, register_2_out_10, register_2_out_11,
       register_2_out_12, register_2_out_13, register_2_out_14, register_2_out_15, register_2_out_16,
       register_2_out_17, register_3_out_10, register_3_out_11, register_3_out_12, register_3_out_13,
       register_3_out_14, register_3_out_15, register_3_out_16, register_3_out_17, register_4_out_10,
       register_4_out_11, register_4_out_12, register_4_out_13, register_4_out_14, register_4_out_15,
       register_4_out_16, register_4_out_17;
  wire [7:0] counter_1_q;

  Clock #(.highDuration(2), .lowDuration(2)) clock_1 (.out(clock_1_out));
  and and_1 (and_1_out, clock_1_out, not_1_out);
  Counter counter_1 (
    .load(in_6), .D({in_11, in_9, in_8, in_7, in_5, in_3, in_2, in_1}), .count(in_17), .Q(counter_1_q),
    .carry(out_27), .clk(and_1_out), .clr(in_20));
  assign controlled_buffer_1_out = in_17 ? register_1_out_17 : 1'bz;  // Controlled_Buffer controlled_buffer_1
  assign controlled_buffer_2_out = in_17 ? register_1_out_16 : 1'bz;  // Controlled_Buffer controlled_buffer_2
  ALU alu_1 (
    .in_1(register_3_out_10), .in_2(register_3_out_11), .in_3(register_3_out_12), .in_4(register_3_out_13),
    .in_5(register_3_out_14), .in_6(register_3_out_15), .in_7(register_3_out_16), .in_8(register_3_out_17),
    .in_9(register_2_out_10), .in_10(register_2_out_11), .in_11(register_2_out_12),
    .in_12(register_2_out_13), .in_13(register_2_out_14), .in_14(register_2_out_15),
    .in_15(register_2_out_16), .in_16(register_2_out_17), .in_17(in_22), .out_18(alu_1_out_18),
    .out_19(alu_1_out_19), .out_20(alu_1_out_20), .out_21(alu_1_out_21), .out_22(alu_1_out_22),
    .out_23(alu_1_out_23), .out_24(alu_1_out_24), .out_25(alu_1_out_25));
  Register register_1 (
    .in_1(clock_2_out), .in_2(alu_1_out_18), .in_3(alu_1_out_19), .in_4(alu_1_out_20), .in_5(alu_1_out_21),
    .in_6(alu_1_out_22), .in_7(alu_1_out_23), .in_8(alu_1_out_24), .in_9(alu_1_out_25),
    .out_10(register_1_out_10), .out_11(register_1_out_11), .out_12(register_1_out_12),
    .out_13(register_1_out_13), .out_14(register_1_out_14), .out_15(register_1_out_15),
    .out_16(register_1_out_16), .out_17(register_1_out_17));
  assign controlled_buffer_3_out = in_17 ? register_1_out_15 : 1'bz;  // Controlled_Buffer controlled_buffer_3
  assign controlled_buffer_4_out = in_17 ? register_1_out_13 : 1'bz;  // Controlled_Buffer controlled_buffer_4
  assign controlled_buffer_5_out = in_17 ? register_1_out_12 : 1'bz;  // Controlled_Buffer controlled_buffer_5
  assign controlled_buffer_6_out = in_17 ? register_1_out_14 : 1'bz;  // Controlled_Buffer controlled_buffer_6
  not not_1 (not_1_out, out_27);
  Clock clock_2 (.out(clock_2_out));
  assign controlled_buffer_7_out = in_17 ? register_1_out_11 : 1'bz;  // Controlled_Buffer controlled_buffer_7
  assign controlled_buffer_8_out = in_17 ? register_1_out_10 : 1'bz;  // Controlled_Buffer controlled_buffer_8
  LED led_1 (.in(controlled_buffer_1_out));
  assign controlled_buffer_8_out = in_4 ? in_10 : 1'bz;  // Controlled_Buffer controlled_buffer_9
  assign controlled_buffer_7_out = in_4 ? in_12 : 1'bz;  // Controlled_Buffer controlled_buffer_10
  assign controlled_buffer_5_out = in_4 ? in_14 : 1'bz;  // Controlled_Buffer controlled_buffer_11
  assign controlled_buffer_4_out = in_4 ? in_15 : 1'bz;  // Controlled_Buffer controlled_buffer_12
  assign controlled_buffer_6_out = in_4 ? in_16 : 1'bz;  // Controlled_Buffer controlled_buffer_13
  assign controlled_buffer_3_out = in_4 ? in_18 : 1'bz;  // Controlled_Buffer controlled_buffer_14
  assign controlled_buffer_2_out = in_4 ? in_19 : 1'bz;  // Controlled_Buffer controlled_buffer_15
  assign controlled_buffer_1_out = in_4 ? in_21 : 1'bz;  // Controlled_Buffer controlled_buffer_16
  LED led_2 (.in(controlled_buffer_2_out));
  LED led_3 (.in(controlled_buffer_6_out));
  LED led_4 (.in(controlled_buffer_4_out));
  LED led_5 (.in(controlled_buffer_3_out));
  LED led_6 (.in(controlled_buffer_7_out));
  LED led_7 (.in(controlled_buffer_8_out));
  LED led_8 (.in(controlled_buffer_5_out));
  and and_2 (and_2_out, in_13, not_1_out);
  assign controlled_buffer_17_out = and_2_out ? controlled_buffer_2_out : 1'bz;  // Controlled_Buffer controlled_buffer_17
  assign controlled_buffer_18_out = and_2_out ? controlled_buffer_1_out : 1'bz;  // Controlled_Buffer controlled_buffer_18
  assign controlled_buffer_2_out = in_23 ? register_2_out_16 : 1'bz;  // Controlled_Buffer controlled_buffer_19
  assign controlled_buffer_1_out = in_23 ? register_2_out_17 : 1'bz;  // Controlled_Buffer controlled_buffer_20
  assign controlled_buffer_21_out = in_24 ? controlled_buffer_1_out : 1'bz;  // Controlled_Buffer controlled_buffer_21
  assign controlled_buffer_22_out = in_24 ? controlled_buffer_2_out : 1'bz;  // Controlled_Buffer controlled_buffer_22
  assign controlled_buffer_1_out = in_26 ? register_3_out_17 : 1'bz;  // Controlled_Buffer controlled_buffer_23
  assign controlled_buffer_2_out = in_26 ? register_3_out_16 : 1'bz;  // Controlled_Buffer controlled_buffer_24
  assign controlled_buffer_25_out = and_2_out ? controlled_buffer_4_out : 1'bz;  // Controlled_Buffer controlled_buffer_25
  assign controlled_buffer_26_out = and_2_out ? controlled_buffer_6_out : 1'bz;  // Controlled_Buffer controlled_buffer_26
  assign controlled_buffer_27_out = and_2_out ? controlled_buffer_5_out : 1'bz;  // Controlled_Buffer controlled_buffer_27
  assign controlled_buffer_28_out = and_2_out ? controlled_buffer_3_out : 1'bz;  // Controlled_Buffer controlled_buffer_28
  Register register_2 (
    .in_1(controlled_buffer_42_out), .in_2(controlled_buffer_43_out), .in_3(controlled_buffer_41_out),
    .in_4(controlled_buffer_27_out), .in_5(controlled_buffer_25_out), .in_6(controlled_buffer_26_out),
    .in_7(controlled_buffer_28_out), .in_8(controlled_buffer_17_out), .in_9(controlled_buffer_18_out),
    .out_10(register_2_out_10), .out_11(register_2_out_11), .out_12(register_2_out_12),
    .out_13(register_2_out_13), .out_14(register_2_out_14), .out_15(register_2_out_15),
    .out_16(register_2_out_16), .out_17(register_2_out_17));
  assign controlled_buffer_6_out = in_23 ? register_2_out_14 : 1'bz;  // Controlled_Buffer controlled_buffer_29
  assign controlled_buffer_3_out = in_23 ? register_2_out_15 : 1'bz;  // Controlled_Buffer controlled_buffer_30
  assign controlled_buffer_5_out = in_23 ? register_2_out_12 : 1'bz;  // Controlled_Buffer controlled_buffer_31
  assign controlled_buffer_4_out = in_23 ? register_2_out_13 : 1'bz;  // Controlled_Buffer controlled_buffer_32
  assign controlled_buffer_33_out = in_24 ? controlled_buffer_5_out : 1'bz;  // Controlled_Buffer controlled_buffer_33
  assign controlled_buffer_34_out = in_24 ? controlled_buffer_4_out : 1'bz;  // Controlled_Buffer controlled_buffer_34
  assign controlled_buffer_35_out = in_24 ? controlled_buffer_6_out : 1'bz;  // Controlled_Buffer controlled_buffer_35
  assign controlled_buffer_36_out = in_24 ? controlled_buffer_3_out : 1'bz;  // Controlled_Buffer controlled_buffer_36
  Register register_3 (
    .in_1(controlled_buffer_46_out), .in_2(controlled_buffer_47_out), .in_3(controlled_buffer_48_out),
    .in_4(controlled_buffer_33_out), .in_5(controlled_buffer_34_out), .in_6(controlled_buffer_35_out),
    .in_7(controlled_buffer_36_out), .in_8(controlled_buffer_22_out), .in_9(controlled_buffer_21_out),
    .out_10(register_3_out_10), .out_11(register_3_out_11), .out_12(register_3_out_12),
    .out_13(register_3_out_13), .out_14(register_3_out_14), .out_15(register_3_out_15),
    .out_16(register_3_out_16), .out_17(register_3_out_17));
  assign controlled_buffer_3_out = in_26 ? register_3_out_15 : 1'bz;  // Controlled_Buffer controlled_buffer_37
  assign controlled_buffer_4_out = in_26 ? register_3_out_13 : 1'bz;  // Controlled_Buffer controlled_buffer_38
  assign controlled_buffer_5_out = in_26 ? register_3_out_12 : 1'bz;  // Controlled_Buffer controlled_buffer_39
  assign controlled_buffer_6_out = in_26 ? register_3_out_14 : 1'bz;  // Controlled_Buffer controlled_buffer_40
  Clock clock_3 (.out(clock_3_out));
  assign controlled_buffer_41_out = and_2_out ? controlled_buffer_7_out : 1'bz;  // Controlled_Buffer controlled_buffer_41
  assign controlled_buffer_42_out = and_2_out ? clock_3_out : 1'bz;  // Controlled_Buffer controlled_buffer_42
  assign controlled_buffer_43_out = and_2_out ? controlled_buffer_8_out : 1'bz;  // Controlled_Buffer controlled_buffer_43
  assign controlled_buffer_7_out = in_23 ? register_2_out_11 : 1'bz;  // Controlled_Buffer controlled_buffer_44
  assign controlled_buffer_8_out = in_23 ? register_2_out_10 : 1'bz;  // Controlled_Buffer controlled_buffer_45
  Clock clock_4 (.out(clock_4_out));
  assign controlled_buffer_46_out = in_24 ? clock_4_out : 1'bz;  // Controlled_Buffer controlled_buffer_46
  assign controlled_buffer_47_out = in_24 ? controlled_buffer_8_out : 1'bz;  // Controlled_Buffer controlled_buffer_47
  assign controlled_buffer_48_out = in_24 ? controlled_buffer_7_out : 1'bz;  // Controlled_Buffer controlled_buffer_48
  assign controlled_buffer_8_out = in_26 ? register_3_out_10 : 1'bz;  // Controlled_Buffer controlled_buffer_49
  assign controlled_buffer_7_out = in_26 ? register_3_out_11 : 1'bz;  // Controlled_Buffer controlled_buffer_50
  Register register_4 (
    .out_10(register_4_out_10), .out_11(register_4_out_11), .out_12(register_4_out_12),
    .out_13(register_4_out_13), .out_14(register_4_out_14), .out_15(register_4_out_15),
    .out_16(register_4_out_16), .out_17(register_4_out_17));  // open: in_1, in_2, in_3, in_4, in_5, in_6, in_7, in_8, in_9
  LED led_9 (.in(register_4_out_10));
  LED led_10 (.in(register_4_out_11));
  LED led_11 (.in(register_4_out_12));
  LED led_12 (.in(register_4_out_13));
  LED led_13 (.in(register_4_out_14));
  LED led_14 (.in(register_4_out_15));
  LED led_15 (.in(register_4_out_16));
  LED led_16 (.in(register_4_out_17));
endmodule

module ALU (
  input  in_1,
  input  in_2,
  input  in_3,
  input  in_4,
  input  in_5,
  input  in_6,
  input  in_7,
  input  in_8,
  input  in_9,
  input  in_10,
  input  in_11,
  input  in_12,
  input  in_13,
  input  in_14,
  input  in_15,
  input  in_16,
  input  in_17,
  output out_18,
  output out_19,
  output out_20,
  output out_21,
  output out_22,
  output out_23,
  output out_24,
  output out_25
);

  wire xor_1_out, xor_2_out, xor_3_out, xor_4_out, xor_5_out, xor_6_out, xor_7_out, xor_8_out;

  xor xor_1 (xor_1_out, in_9, in_17);
  xor xor_2 (xor_2_out, in_10, in_17);
  xor xor_3 (xor_3_out, in_11, in_17);
  xor xor_4 (xor_4_out, in_12, in_17);
  xor xor_5 (xor_5_out, in_13, in_17);
  xor xor_6 (xor_6_out, in_14, in_17);
  xor xor_7 (xor_7_out, in_15, in_17);
  xor xor_8 (xor_8_out, in_16, in_17);
  ADDER adder_1 (
    .in_1(in_17), .in_2(in_1), .in_3(in_2), .in_4(in_3), .in_5(in_4), .in_6(in_5), .in_7(in_6), .in_8(in_7),
    .in_9(in_8), .in_10(xor_1_out), .in_11(xor_2_out), .in_12(xor_3_out), .in_13(xor_4_out),
    .in_14(xor_5_out), .in_15(xor_6_out), .in_16(xor_7_out), .in_17(xor_8_out), .out_18(out_18),
    .out_19(out_19), .out_20(out_20), .out_21(out_21), .out_22(out_22), .out_23(out_23), .out_24(out_24),
    .out_25(out_25));
endmodule

module ADDER (
  input  in_1,
  input  in_2,
  input  in_3,
  input  in_4,
  input  in_5,
  input  in_6,
  input  in_7,
  input  in_8,
  input  in_9,
  input  in_10,
  input  in_11,
  input  in_12,
  input  in_13,
  input  in_14,
  input  in_15,
  input  in_16,
  input  in_17,
  output out_18,
  output out_19,
  output out_20,
  output out_21,
  output out_22,
  output out_23,
  output out_24,
  output out_25
);

  wire n1_bit_adder_1_out_5, n1_bit_adder_2_out_5, n1_bit_adder_3_out_5, n1_bit_adder_4_out_5,
       n1_bit_adder_5_out_5, n1_bit_adder_6_out_5, n1_bit_adder_7_out_5;

  _1_bit_adder u_1_bit_adder_1 (.carry(in_1), ._1(in_2), ._2(in_10), .out_4(out_18), .out_5(n1_bit_adder_1_out_5));
  _1_bit_adder u_1_bit_adder_2 (
    .carry(n1_bit_adder_1_out_5), ._1(in_3), ._2(in_11), .out_4(out_19), .out_5(n1_bit_adder_2_out_5));
  _1_bit_adder u_1_bit_adder_3 (
    .carry(n1_bit_adder_2_out_5), ._1(in_4), ._2(in_12), .out_4(out_20), .out_5(n1_bit_adder_3_out_5));
  _1_bit_adder u_1_bit_adder_4 (
    .carry(n1_bit_adder_3_out_5), ._1(in_5), ._2(in_13), .out_4(out_21), .out_5(n1_bit_adder_4_out_5));
  _1_bit_adder u_1_bit_adder_5 (
    .carry(n1_bit_adder_4_out_5), ._1(in_6), ._2(in_14), .out_4(out_22), .out_5(n1_bit_adder_5_out_5));
  _1_bit_adder u_1_bit_adder_6 (
    .carry(n1_bit_adder_5_out_5), ._1(in_7), ._2(in_15), .out_4(out_23), .out_5(n1_bit_adder_6_out_5));
  _1_bit_adder u_1_bit_adder_7 (
    .carry(n1_bit_adder_6_out_5), ._1(in_8), ._2(in_16), .out_4(out_24), .out_5(n1_bit_adder_7_out_5));
  _1_bit_adder u_1_bit_adder_8 (.carry(n1_bit_adder_7_out_5), ._1(in_9), ._2(in_17), .out_4(out_25));  // open: out_5
endmodule

module _1_bit_adder (
  input  carry,
  input  _1,
  input  _2,
  output out_4,
  output out_5
);

  wire and_1_out, and_2_out, xor_1_out;

  xor xor_1 (xor_1_out, _1, _2);
  and and_1 (and_1_out, _1, _2);
  xor xor_2 (out_4, xor_1_out, carry);
  and and_2 (and_2_out, xor_1_out, carry);
  or or_1 (out_5, and_2_out, and_1_out);
endmodule

module BUS (
  input  in_1,
  input  in_2,
  input  in_3,
  input  in_4,
  input  in_5,
  input  in_6,
  input  in_7,
  input  in_8,
  output out_9,
  output out_10,
  output out_11,
  output out_12,
  output out_13,
  output out_14,
  output out_15
);

  D_Flip_Flop d_ff_1 (.clk(in_1), .D(in_2), .Q(out_9));  // open: Qn, preset, en, reset
  D_Flip_Flop d_ff_2 (.clk(in_1), .D(in_3), .Q(out_10));  // open: Qn, preset, en, reset
  D_Flip_Flop d_ff_3 (.clk(in_1), .D(in_4), .Q(out_11));  // open: Qn, preset, en, reset
  D_Flip_Flop d_ff_4 (.clk(in_1), .D(in_5), .Q(out_12));  // open: Qn, preset, en, reset
  D_Flip_Flop d_ff_5 (.clk(in_1), .D(in_6), .Q(out_13));  // open: Qn, preset, en, reset
  D_Flip_Flop d_ff_6 (.clk(in_1), .D(in_7), .Q(out_14));  // open: Qn, preset, en, reset
  D_Flip_Flop d_ff_7 (.clk(in_1), .D(in_8), .Q(out_15));  // open: Qn, preset, en, reset
endmodule

module Register (
  input  in_1,
  input  in_2,
  input  in_3,
  input  in_4,
  input  in_5,
  input  in_6,
  input  in_7,
  input  in_8,
  input  in_9,
  output out_10,
  output out_11,
  output out_12,
  output out_13,
  output out_14,
  output out_15,
  output out_16,
  output out_17
);

  D_Flip_Flop d_ff_1 (.clk(in_1), .D(in_2), .Q(out_10));  // open: Qn, preset, en, reset
  D_Flip_Flop d_ff_2 (.clk(in_1), .D(in_3), .Q(out_11));  // open: Qn, preset, en, reset
  D_Flip_Flop d_ff_3 (.clk(in_1), .D(in_4), .Q(out_12));  // open: Qn, preset, en, reset
  D_Flip_Flop d_ff_4 (.clk(in_1), .D(in_5), .Q(out_13));  // open: Qn, preset, en, reset
  D_Flip_Flop d_ff_5 (.clk(in_1), .D(in_6), .Q(out_14));  // open: Qn, preset, en, reset
  D_Flip_Flop d_ff_6 (.clk(in_1), .D(in_7), .Q(out_15));  // open: Qn, preset, en, reset
  D_Flip_Flop d_ff_7 (.clk(in_1), .D(in_8), .Q(out_16));  // open: Qn, preset, en, reset
  D_Flip_Flop d_ff_8 (.clk(in_1), .D(in_9), .Q(out_17));  // open: Qn, preset, en, reset
endmodule
